# Fritzing sketch Circuit (saved by Fritzing 0.9.10b)

parts:
  U1 = ESP8266 NodeMCU LoLin base
  Part1 = LCD1602-I2C
  DHT1 = Humidity and Temperature Sensor DHT11
  A1 = 2 channel relay module [package=THT]
  A2 = 2 channel relay module [package=THT]

nets:
  N1: U1.GND1-0, U1.GND1-1, U1.GND2-3, U1.GND3-3, Part1.GND, DHT1.GND_2, A1.pin_14, A2.pin_14
  N2: U1.D1-0, U1.D1-2, Part1.SCL
  N3: U1.D2-0, U1.D2-1, Part1.SDA
  N4: U1.D5-1, U1.D5-2, U1.D5-3, A2.pin_15, A2.pin_16
  N5: U1.D6-0, U1.D6-1, U1.D6-3, A1.pin_15, A1.pin_16
  N6: U1.A0, DHT1.Data-signal
  VCC: U1.VIN, U1.5V-0, U1.5V-2, Part1.VCC, DHT1.Vcc, A1.pin_13, A2.pin_13

custom parts:
  ESP8266 NodeMCU LoLin base: ESP8266 based NodeMCU Base
  LCD1602-I2C: A standard character display, usually with 2x16 characters. Comes in many colors with LCM1602 IIC attached.
  Humidity and Temperature Sensor DHT11: Digital relative humidity & temperature sensor DHT11
  2 channel relay module: 2 channel Relay Module 5V 12V 24V High and Low Level Trigger Relay Control With Optocoupler Two Way relays DC 5 V 12 V 24 V Volt.
